# Fritzing sketch schematic (saved by Fritzing 0.9.4)
circuit board: 7.6983cm x 5.73367cm
breadboards: 1

parts:
  LDR = Photocell (LDR) [package=THT]
  BMP180 = Barometric Pressure Sensor - BMP180 Breakout (GY-68)
  DHT11 = Humidity and Temperature Sensor DHT11
  R_LDR = Resistor [tolerance=±5% resistance=10k package="0805 [SMD]"]
  R = Resistor [tolerance=±5% resistance=10k package="0805 [SMD]"]
  U1 = LuaNode32 / ESP32

nets:
  N1: LDR.pin_0, R_LDR.Pin_1, U1.D34
  VCC: LDR.pin_1, BMP180.VCC, DHT11.Vcc, R.Pin_1, U1.3V3
  GND: BMP180.GND, DHT11.GND, R_LDR.Pin_0, U1.GND
  N2: BMP180.SCL, BMP180.SDA, U1.D35, U1.D27
  N3: DHT11.Data, R.Pin_0, U1.D13

custom parts:
  Humidity and Temperature Sensor DHT11: Digital relative humidity & temperature sensor DHT11
  LuaNode32 / ESP32: ESP32 based LuaNode32
